# Fritzing sketch NEW (saved by Fritzing 1.0.5)

parts:
  Load_Cell1 = Load Cell - Red/white/black/green
  M1 = BTS7960
  M3 = DC Mini Metal Gear Motor
  M7 = DC Mini Metal Gear Motor
  Load_Cell2 = Load Cell - Red/white/black/green
  Load_Cell3 = Load Cell - Red/white/black/green
  M2 = BTS7960
  M8 = DC Mini Metal Gear Motor
  M9 = BTS7960
  V1 = DC Power Supply [voltage=12V internal_resistance=1Ω max_current=0.1A]
  Matrix_keypad1 = KEYPAD 4x4
  LCD2 = LCD screen
  LCM1602_IIC1 = LCM1602 IIC [part_number="LCM1602 IIC" chip_label="LCM1602 IIC" package="DIP (Dual Inline) [THT]"]
  Part2 = HX711 Weighing Sensor Module
  Part3 = HX711 Weighing Sensor Module
  Part1 = HX711 Weighing Sensor Module
  U3 = ESP32-38PinWide [part_number=ESP32-38PinWide]
  PART1 = SparkFun Soil Moisture Sensor [part_number=SEN-13322]
  Part4 = HX711 Weighing Sensor Module
  Load_Cell4 = Load Cell - Red/white/black/green
  Part5 = Arduino Mega 2560 (Rev3)
  DS1 = DS18B20 1-Wire Temperature Sensor Probe
  M10 = BTS7960

nets:
  N1: Load_Cell1.wire1, Part1.E+
  N2: Load_Cell1.wire2, Part1.A-
  N3: Load_Cell1.wire3, Part1.E-
  N4: Load_Cell1.wire4, Part1.A+
  N5: M1.pin1, Part5.D5_PWM
  N6: M1.pin2, Part5.D4_PWM
  N7: M1.pin3, Part5.D41
  N8: M1.pin4, Part5.D39
  VCC: M1.pin7, M2.pin7, M9.pin7, Part2.VCC, Part3.VCC, Part1.VCC, Part4.VCC, Part5.5V, M10.pin7
  GND: M1.pin8, M2.pin8, M9.pin8, Part2.GND, Part3.GND, Part1.GND, PART1.GND, Part4.GND, Part5.GND, DS1.GND, M10.pin8
  N9: M1.pin9, M2.pin9, M9.pin9, V1.Pin_1
  N10: M1.pin10, M2.pin10, M9.pin10, V1.Pin_2
  N11: M1.pin11, M3.IN2
  N12: M1.pin12, M3.IN1
  N13: M7.IN1, M2.pin12
  N14: M7.IN2, M2.pin11
  N15: Load_Cell2.wire1, Part3.E+
  N16: Load_Cell2.wire2, Part3.A-
  N17: Load_Cell2.wire3, Part3.E-
  N18: Load_Cell2.wire4, Part3.A+
  N19: Load_Cell3.wire1, Part2.E+
  N20: Load_Cell3.wire2, Part2.A-
  N21: Load_Cell3.wire3, Part2.E-
  N22: Load_Cell3.wire4, Part2.A+
  N23: M2.pin1, Part5.D6_PWM
  N24: M2.pin2, Part5.D7_PWM
  N25: M2.pin3, Part5.D38
  N26: M2.pin4, Part5.D40
  N27: M8.IN1, M9.pin12
  N28: M8.IN2, M9.pin11
  N29: M9.pin1, Part5.D3_PWM
  N30: M9.pin2, Part5.D2_PWM
  N31: M9.pin3, Part5.D36
  N32: M9.pin4, Part5.D37
  N33: Matrix_keypad1.col1, U3.GPIO4
  N34: Matrix_keypad1.col2, U3.GPIO16
  N35: Matrix_keypad1.col3, U3.GPIO17
  N36: Matrix_keypad1.col4, U3.GPIO5
  N37: Matrix_keypad1.row1, U3.GPIO18
  N38: Matrix_keypad1.row2, U3.GPIO19
  N39: Matrix_keypad1.row3, U3.GPIO21
  N40: Matrix_keypad1.row4, U3.GPIO33
  VSS: LCD2.VSS, LCM1602_IIC1.VSS
  VDD: LCD2.VDD, LCM1602_IIC1.VDD
  N41: LCD2.V0, LCM1602_IIC1.V0
  N42: LCD2.RS, LCM1602_IIC1.RS
  N43: LCD2.R/W, LCM1602_IIC1.RW
  N44: LCD2.E, LCM1602_IIC1.E
  N45: LCD2.DB0, LCM1602_IIC1.D0
  N46: LCD2.DB1, LCM1602_IIC1.D1
  N47: LCD2.DB2, LCM1602_IIC1.D2
  N48: LCD2.DB3, LCM1602_IIC1.D3
  N49: LCD2.DB4, LCM1602_IIC1.D4
  N50: LCD2.DB5, LCM1602_IIC1.D5
  N51: LCD2.DB6, LCM1602_IIC1.D6
  N52: LCD2.DB7, LCM1602_IIC1.D7
  N53: LCD2.LED+, LCM1602_IIC1.A
  N54: LCD2.LED-, LCM1602_IIC1.K
  N55: LCM1602_IIC1.GND, U3.GPIO11
  VCC_2: LCM1602_IIC1.VCC, U3.VIN
  N56: LCM1602_IIC1.SDA, U3.GPIO23
  N57: LCM1602_IIC1.SCL, U3.GPIO22
  N58: Part2.DO/RX, Part5.D27
  N59: Part2.CK/TX, Part5.D26
  N60: Part3.CK/TX, Part5.D28, Part5.D31
  N61: Part1.DO/RX, Part5.D49
  N62: Part1.CK/TX, Part5.D50
  N63: U3.GPIO26, Part5.D16_PWM/TX2
  N64: U3.GPIO27, Part5.D17_PWM/RX2
  VCC_3: PART1.VCC, Part5.3V3, DS1.VDD
  N65: PART1.SIG, Part5.A0
  N66: Part4.DO/RX, Part5.D22
  N67: Part4.CK/TX, Part5.D23
  N68: Part4.E+, Load_Cell4.wire1
  N69: Part4.E-, Load_Cell4.wire3
  N70: Part4.A+, Load_Cell4.wire4
  N71: Part4.A-, Load_Cell4.wire2
  N72: Part5.D9_PWM, M10.pin1
  N73: Part5.D8_PWM, M10.pin2
  N74: Part5.D34, M10.pin3
  N75: Part5.D35, M10.pin4
  N76: Part5.D52, DS1.DQ

notes:
  rice husk
  One enclosed 12 V 15 A With fuses
  Wood ash
  Compost
  Enable Wifi communication
  LCD
  DS18B20 Temp sensor
  Sensors
  Water pump

custom parts:
  Load Cell - Red/white/black/green: A rectangle load cell/weighting pressure Sensor with four wires - Red, white, black, green. Normally corresponding with E+, E-, A+, A- respectively.
  BTS7960: BTS7960 43A Peak Power H-Bridge PWM Motor Driver
  KEYPAD 4x4: Matrix keypad 16 buttons, 4 rows x 4 columns
  LCM1602 IIC: I2C-Module to use a 1602 or 2004 LCD on with the wire.h libory Serial LCD Modul
  ESP32-38PinWide: Generic 38-Pin ESP32 with wide format (only access to one side of pins on a breadboard) based on Stephen Lilley's HiLetgo ESP-WROOM-32 ESP32 ESP-32S Development Board.
  SparkFun Soil Moisture Sensor: The SparkFun Soil Moisture Sensor is a simple breakout for measuring the moisture in soil and similar materials.
