# Fritzing sketch updateThesis (saved by Fritzing 1.0.5)

parts:
  Load_Cell1 = Load Cell - Red/white/black/green
  U1 = ESP32-38PinWide [part_number=ESP32-38PinWide]
  M1 = BTS7960
  M3 = DC Mini Metal Gear Motor
  M7 = DC Mini Metal Gear Motor
  Load_Cell2 = Load Cell - Red/white/black/green
  Load_Cell3 = Load Cell - Red/white/black/green
  M2 = BTS7960
  M8 = DC Mini Metal Gear Motor
  M9 = BTS7960
  S1 = H-Bridge with L298N
  V1 = DC Power Supply [voltage=12V internal_resistance=1Ω max_current=0.1A]
  Matrix_keypad1 = KEYPAD 4x4
  LCD2 = LCD screen
  LCM1602_IIC1 = LCM1602 IIC [part_number="LCM1602 IIC" chip_label="LCM1602 IIC" package="DIP (Dual Inline) [THT]"]
  M11 = BTS7960
  Part2 = HX711 Weighing Sensor Module
  Part3 = HX711 Weighing Sensor Module
  Part1 = HX711 Weighing Sensor Module
  M12 = DC Mini Metal Gear Motor
  U3 = ESP32-38PinWide [part_number=ESP32-38PinWide]
  M6 = gear-motor

nets:
  N1: Load_Cell1.wire1, Part1.E+
  N2: Load_Cell1.wire2, Part1.A-
  N3: Load_Cell1.wire3, Part1.E-
  N4: Load_Cell1.wire4, Part1.A+
  N5: U1.GPIO34, Part1.DO/RX
  N6: U1.GPIO35, Part1.CK/TX
  N7: U1.GPIO32, Part3.DO/RX
  N8: U1.GPIO33, Part3.CK/TX
  N9: U1.GPIO25, Part2.DO/RX
  N10: U1.GPIO26, U3.GPIO27
  N11: U1.GPIO27, U3.GPIO26
  N12: U1.GPIO14, Part2.CK/TX
  GND: U1.GND, M1.pin9, M2.pin9, M9.pin9, S1.GND, V1.Pin_1, M11.pin11, U3.GND
  GND_2: U1.GPIO11, Part2.GND, Part3.GND, Part1.GND
  VCC: U1.VIN, Part2.VCC, Part3.VCC, Part1.VCC
  N13: U1.GPIO2, M1.pin3, M2.pin3, M9.pin3
  N14: U1.GPIO0, M1.pin1
  N15: U1.GPIO4, M9.pin1
  N16: U1.GPIO16, M2.pin1
  N17: U1.GPIO21, S1.ENA
  N18: U1.GPIO22, S1.IN2
  N19: U1.GPIO23, S1.IN1
  N20: M1.pin7, M2.pin7, M9.pin7
  N21: M1.pin8, M2.pin8, M9.pin8
  N22: M1.pin10, M2.pin10, M9.pin10, S1.12V, V1.Pin_2, M11.pin12
  N23: M1.pin11, M3.IN2
  N24: M1.pin12, M3.IN1
  N25: M7.IN1, M2.pin12
  N26: M7.IN2, M2.pin11
  N27: Load_Cell2.wire1, Part3.E+
  N28: Load_Cell2.wire2, Part3.A-
  N29: Load_Cell2.wire3, Part3.E-
  N30: Load_Cell2.wire4, Part3.A+
  N31: Load_Cell3.wire1, Part2.E+
  N32: Load_Cell3.wire2, Part2.A-
  N33: Load_Cell3.wire3, Part2.E-
  N34: Load_Cell3.wire4, Part2.A+
  N35: M8.IN1, M9.pin12
  N36: M8.IN2, M9.pin11
  N37: S1.ENB, S1.ENB-5V
  N38: S1.M1-01, M6.pin_1
  N39: S1.M1-02, M6.pin_2
  N40: Matrix_keypad1.col1, U3.GPIO4
  N41: Matrix_keypad1.col2, U3.GPIO16
  N42: Matrix_keypad1.col3, U3.GPIO17
  N43: Matrix_keypad1.col4, U3.GPIO5
  N44: Matrix_keypad1.row1, U3.GPIO18
  N45: Matrix_keypad1.row2, U3.GPIO19
  N46: Matrix_keypad1.row3, U3.GPIO21
  N47: Matrix_keypad1.row4, U3.GPIO14
  VSS: LCD2.VSS, LCM1602_IIC1.VSS
  VDD: LCD2.VDD, LCM1602_IIC1.VDD
  N48: LCD2.V0, LCM1602_IIC1.V0
  N49: LCD2.RS, LCM1602_IIC1.RS
  N50: LCD2.R/W, LCM1602_IIC1.RW
  N51: LCD2.E, LCM1602_IIC1.E
  N52: LCD2.DB0, LCM1602_IIC1.D0
  N53: LCD2.DB1, LCM1602_IIC1.D1
  N54: LCD2.DB2, LCM1602_IIC1.D2
  N55: LCD2.DB3, LCM1602_IIC1.D3
  N56: LCD2.DB4, LCM1602_IIC1.D4
  N57: LCD2.DB5, LCM1602_IIC1.D5
  N58: LCD2.DB6, LCM1602_IIC1.D6
  N59: LCD2.DB7, LCM1602_IIC1.D7
  N60: LCD2.LED+, LCM1602_IIC1.A
  N61: LCD2.LED-, LCM1602_IIC1.K
  N62: LCM1602_IIC1.GND, M11.pin8, U3.GPIO11
  VCC_2: LCM1602_IIC1.VCC, U3.VIN
  N63: LCM1602_IIC1.SDA, U3.GPIO22
  N64: LCM1602_IIC1.SCL, U3.GPIO23
  N65: M11.pin1, U3.GPIO34
  N66: M11.pin3, U3.GPIO35
  N67: M11.pin7, U3.3.3
  N68: M11.pin9, M12.IN2
  N69: M11.pin10, M12.IN1

notes:
  K auger
  One enclosed 12 V 15 A With fuses
  N auger
  P auger
  Enable Wifi communication
  to bucket enable drop
  Mixer
  Sensors

custom parts:
  Load Cell - Red/white/black/green: A rectangle load cell/weighting pressure Sensor with four wires - Red, white, black, green. Normally corresponding with E+, E-, A+, A- respectively.
  ESP32-38PinWide: Generic 38-Pin ESP32 with wide format (only access to one side of pins on a breadboard) based on Stephen Lilley's HiLetgo ESP-WROOM-32 ESP32 ESP-32S Development Board.
  BTS7960: BTS7960 43A Peak Power H-Bridge PWM Motor Driver
  H-Bridge with L298N: h-bridge
  KEYPAD 4x4: Matrix keypad 16 buttons, 4 rows x 4 columns
  LCM1602 IIC: I2C-Module to use a 1602 or 2004 LCD on with the wire.h libory Serial LCD Modul
